# Fritzing sketch esquema_roi (saved by Fritzing 0.9.3b)
breadboards: 1

parts:
  Mod1 = Raspberry Pi Pico W
  Part1 = KY-019 5V Relay Module [package="Breakout board"]
  J1 = Basic Servo
  VCC1 = Battery
  Part2 = KY-015 Temperature & Humidity Sensor Module [package="Breakout board"]
  Part3 = LCD1602-I2C
  F1 = Fan - Ventilador [package=THT]
  LED1 = RGB LED - (4 legs) [package="5 mm [THT]"]
  R1 = Photocell (LDR) [package=THT]
  S1 = Pushbutton [package="[THT]"]
  S2 = Pushbutton [package="[THT]"]
  J2 = Basic Servo
  R2 = Resistor [tolerance=±5% resistance=10k package="1206 [SMD]"]
  R3 = Resistor [tolerance=±5% resistance=220 package="1206 [SMD]"]

nets:
  N1: Mod1.pin_1, Part3.SCL
  N2: Mod1.pin_2, Part3.SDA
  N3: Mod1.pin_3, Mod1.pin_8, Mod1.pin_13, Mod1.pin_18, Mod1.pin_23, Mod1.pin_28, Mod1.pin_33, Mod1.pin_38, Mod1.pin_42, LED1.red_cathode
  N4: Mod1.pin_4, J1.pulse
  N5: Mod1.pin_5, J2.pulse
  N6: Mod1.pin_6, Part2.S
  N7: Mod1.pin_10, Part1.S
  N8: Mod1.pin_21, LED1.blue_cathode
  N9: Mod1.pin_22, LED1.common_anode
  N10: Mod1.pin_26, S2.Pin_1, S2.Pin_2
  N11: Mod1.pin_27, S1.Pin_1, S1.Pin_2
  N12: Mod1.pin_34, R1.pin_1, R2.Pin_0
  VCC: Part1.+, Part1.NO, J1.vcc, VCC1.-, VCC1.+, Part2.Vin, Part3.VCC, R1.pin_0, J2.vcc
  GND: Part1.-, J1.gnd, Part2.-, Part3.GND, F1.GND, S1.Pin_3, S1.Pin_4, S2.Pin_3, S2.Pin_4, J2.gnd, R2.Pin_1, R3.Pin_1
  N13: Part1.Common, F1.5V
  N14: LED1.green_cathode, R3.Pin_0

custom parts:
  Raspberry Pi Pico W: Raspberry Pi Pico W. Based around the RP2040 microcontroller the Pico W is a low cost microcontroller device bringing Raspberry Pi quality, cost, and easy of use to the microcontroller space. The areas marked KEEPOUT in pcb silkscreen should not have traces running through them to avoid shorts on a soldered in module!
  KY-019 5V Relay Module: KY-019 5V Relay module, used to control AC circuits.
  Battery: Your standard 2x 18650 battery pack (7,4 Volts)
  KY-015 Temperature & Humidity Sensor Module: KY-015 temperature and humidity sensor module, provides a low-latency serial interface to measure humidity and temperature.
  LCD1602-I2C: A standard character display, usually with 2x16 characters. Comes in many colors with LCM1602 IIC attached.
  Fan - Ventilador: Ventilador de 2 pines, se encuentra comunmente en computadoras de escritorio
